# Fritzing sketch lady_lacelove (saved by Fritzing 0.9.4)
circuit board: 9.39755cm x 4.11289cm

parts:
  IC1 = ULN2003A [package="DIP16 [THT]"]
  U1 = 74HC595 [package="DIP16 [THT]"]
  U2 = 74HC595 [package="DIP16 [THT]"]
  U3 = 74HC595 [package="DIP16 [THT]"]
  IC3 = ULN2003A [package="DIP16 [THT]"]
  IC4 = ULN2003A [package="DIP16 [THT]"]
  MOTOR1 = prefix101206
  MOTOR2 = prefix101206
  MOTOR4 = prefix101206
  MOTOR6 = prefix101206
  IC6 = ULN2003A [package="DIP16 [THT]"]
  MOTOR8 = prefix101206
  MOTOR7 = prefix101206
  J1 = female pin header, 2 pins [form="♀ (female)"]
  U4 = 74HC595 [package="DIP16 [THT]"]
  toArduino = molex pin header, 5 pins [form=molex]

nets:
  N1: IC1.In_1, U1.Q7
  N2: IC1.In_2, U1.Q6
  N3: IC1.In_3, U1.Q5
  N4: IC1.In_4, U1.Q4
  N5: IC1.In_5, U1.Q3
  N6: IC1.In_6, U1.Q2
  N7: IC1.In_7, U1.Q1
  GND: IC1.0V, U1.GND, U1.OE, U2.GND, U2.OE, U3.GND, U3.OE, IC3.0V, IC4.0V, IC6.0V, J1.pin2, U4.GND, U4.OE, toArduino.pin4
  12V: IC1.COM_-_Common, IC3.COM_-_Common, IC4.COM_-_Common, MOTOR1.connector1, MOTOR2.connector1, MOTOR4.connector1, MOTOR6.connector1, IC6.COM_-_Common, MOTOR8.connector1, MOTOR7.connector1, J1.pin1
  N8: IC1.Out_7, MOTOR2.connector5
  N9: IC1.Out_4, MOTOR4.connector2
  N10: IC1.Out_3, MOTOR4.connector3
  N11: IC1.Out_2, MOTOR4.connector4
  N12: IC1.Out_1, MOTOR4.connector5
  N13: U1.Q7', U3.DS
  5V: U1.MR, U1.VCC, U2.MR, U2.VCC, U3.MR, U3.VCC, U4.MR, U4.VCC, toArduino.pin1
  CLOCK/LATCH: U1.SH_CP, U1.ST_CP, U2.SH_CP, U2.ST_CP, U3.SH_CP, U3.ST_CP, U4.SH_CP, U4.ST_CP, toArduino.pin2, toArduino.pin3
  N14: U1.DS, U4.Q7'
  N15: U2.Q1, IC6.In_7
  N16: U2.Q2, IC6.In_6
  N17: U2.Q3, IC6.In_5
  N18: U2.Q4, IC6.In_4
  N19: U2.Q5, IC6.In_3
  N20: U2.Q6, IC6.In_2
  N21: U2.Q7, IC6.In_1
  N22: U2.Q7', U4.DS
  DATA: U2.DS, toArduino.pin5
  N23: U3.Q1, IC3.In_7
  N24: U3.Q2, IC3.In_6
  N25: U3.Q3, IC3.In_5
  N26: U3.Q4, IC3.In_4
  N27: U3.Q5, IC3.In_3
  N28: U3.Q6, IC3.In_2
  N29: U3.Q7, IC3.In_1
  N30: IC3.Out_7, MOTOR6.connector2
  N31: IC3.Out_6, MOTOR6.connector3
  N32: IC3.Out_5, MOTOR6.connector4
  N33: IC3.Out_4, MOTOR6.connector5
  N34: IC3.Out_3, MOTOR2.connector2
  N35: IC3.Out_2, MOTOR2.connector3
  N36: IC3.Out_1, MOTOR2.connector4
  N37: IC4.In_1, U4.Q7
  N38: IC4.In_2, U4.Q6
  N39: IC4.In_3, U4.Q5
  N40: IC4.In_4, U4.Q4
  N41: IC4.In_5, U4.Q3
  N42: IC4.In_6, U4.Q2
  N43: IC4.In_7, U4.Q1
  N44: IC4.Out_7, MOTOR8.connector2
  N45: IC4.Out_6, MOTOR8.connector3
  N46: IC4.Out_5, MOTOR8.connector4
  N47: IC4.Out_4, MOTOR8.connector5
  N48: IC4.Out_1, MOTOR1.connector2
  N49: MOTOR1.connector3, IC6.Out_7
  N50: MOTOR1.connector4, IC6.Out_6
  N51: MOTOR1.connector5, IC6.Out_5
  N52: IC6.Out_4, MOTOR7.connector2
  N53: IC6.Out_3, MOTOR7.connector3
  N54: IC6.Out_2, MOTOR7.connector4
  N55: IC6.Out_1, MOTOR7.connector5

notes:
  12 V
  5v
  595->
  data (14)-Q`(9) - cyan
  latch-latch (13) - gris
  clock-clock (11) - ocre
  data- pin8
  latch - pin 12
  clock - pin12
